// Logisim project DSD_Lab_06.circ as structural Verilog: 1 circuit, main circuit main
module main (
  input  X0,
  input  Y0,
  input  C0,
  input  X1,
  input  Y1,
  input  X2,
  input  Y2,
  input  X3,
  input  Y3,
  output out_10,
  output out_11,
  output out_12,
  output out_13,
  output out_14
);

  wire C1_out, C2_out, C3_out, G0_out, G1_out, G2_out, G3_out, P0_out, P0C0_out, P1_out, P1G0_out,
       P1P0C0_out, P2_out, P2G1_out, P2P1G0_out, P2P1P0C0_out, P3_out, P3G2_out, P3P2G1_out, P3P2P1G0_out,
       P3P2P1P0C0_out;

  xor P0 (P0_out, X0, Y0);
  xor P1 (P1_out, X1, Y1);
  and G1 (G1_out, X1, Y1);
  xor P2 (P2_out, X2, Y2);
  and G2 (G2_out, X2, Y2);
  xor P3 (P3_out, X3, Y3);
  and G3 (G3_out, X3, Y3);
  and P3G2 (P3G2_out, G2_out, P3_out);
  xor S0 (out_14, P0_out, C0);
  and P0C0 (P0C0_out, C0, P0_out);
  and G0 (G0_out, X0, Y0);
  xor S1 (out_13, P1_out, C1_out);
  and P2G1 (P2G1_out, P2_out, G1_out);
  and P3P2G1 (P3P2G1_out, P3_out, P2_out, G1_out);
  and P3P2P1G0 (P3P2P1G0_out, P3_out, P2_out, P0_out, G0_out);
  and P3P2P1P0C0 (P3P2P1P0C0_out, P3_out, C0, P2_out, P0_out, P0_out);
  and P1G0 (P1G0_out, P1_out, G0_out);
  and P1P0C0 (P1P0C0_out, C0, P0_out, P1_out);
  xor S2 (out_12, P2_out, C2_out);
  and P2P1G0 (P2P1G0_out, P2_out, P1_out, G0_out);
  and P2P1P0C0 (P2P1P0C0_out, P2_out, P1_out, P0_out, C0);
  or C1 (C1_out, P0C0_out, G0_out);
  xor S3 (out_11, P3_out, C3_out);
  or C2 (C2_out, G1_out, P1G0_out, P1P0C0_out);
  or C4 (out_10, G3_out, P3G2_out, P3P2P1P0C0_out, P3P2P1G0_out, P3P2G1_out);
  or C3 (C3_out, P2G1_out, G2_out, P2P1G0_out, P2P1P0C0_out);

  // Notes on the sheet:
  //   Carry
  //   Sum
endmodule
